# Fritzing sketch circuit (saved by Fritzing 0.9.5d)

parts:
  Part1 = Adafruit Feather HUZZAH ESP8266 [part_number="Adafruit #2821"]
  DFRobot_DFPlayer_Mini1 = DFRobot DFPlayer Mini [part_number=DFR0299]
  Part2 = PN532 Elechouse RFID NFC Module V3
  SPKR2 = Loudspeaker
  R1 = Resistor [tolerance=±5% resistance=1k package=THT]
  S1 = Toggle Switch [package=THT]
  U1 = LIPO-110mAh [package=lipo-110]

nets:
  GND: Part1.GND, DFRobot_DFPlayer_Mini1.GND-1, Part2.GND
  VCC: Part1.3.3V, DFRobot_DFPlayer_Mini1.VCC, Part2.VCC
  N1: Part1.GPIO14/SCK, DFRobot_DFPlayer_Mini1.TX
  N2: Part1.GPIO13/MOSI, R1.Pin_0
  N3: Part1.GPIO5/SCL, Part2.SCL
  N4: Part1.GPIO4/SDA, Part2.SDA
  N5: DFRobot_DFPlayer_Mini1.RX, R1.Pin_1
  N6: DFRobot_DFPlayer_Mini1.SPK_1, SPKR2.pin1
  N7: DFRobot_DFPlayer_Mini1.SPK_2, SPKR2.pin2
  N8: S1.COM, U1.+

custom parts:
  Adafruit Feather HUZZAH ESP8266: his is the Adafruit Feather HUZZAH ESP8266 - our take on an 'all-in-one' ESP8266 WiFi development board with built in USB and battery charging. Its an ESP8266 WiFi module with all the extras you need, ready to rock! We have other boards in the Feather family, check'em out here. At the Feather HUZZAH's heart is an ESP8266 WiFi microcontroller clocked at 80 MHz and at 3.3V logic. This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
  PN532 Elechouse RFID NFC Module V3: NFC is a popular technology in recent years. We often heard this work while smart phone company such as Samsung or HTC introduces their latest high-end phones. Almost all the high-end phone in the market support NFC. Near field communication (NFC) is a set of standards for smart phones and similar devices to establish radio communication with each other by touching them together or bringing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
